# Fritzing sketch sensor-luminosidade-protoboard (saved by Fritzing 0.9.3b)
breadboards: 1

parts:
  Componente1 = Arduino Uno (Rev3)
  LED1 = LED - 3mm [color="Red (633nm)" package="3 mm [THT]"]
  R1 = Resistor [tolerance=±10% resistance=330 package="2010 [SMD]"]
  R2 = Photocell (LDR) [package=THT]
  R3 = Resistor [tolerance=±10% resistance=10k package="2010 [SMD]"]

nets:
  N1: Componente1.A5/SCL, R2.pin_1, R3.Pin_0
  N2: Componente1.D10_PWM/SS, LED1.cathode
  N3: Componente1.5V, R3.Pin_1
  N4: Componente1.GND, R1.Pin_1, R2.pin_0
  N5: LED1.anode, R1.Pin_0
